# Fritzing sketch sketch (saved by Fritzing 0.9.3b)
breadboards: 1

parts:
  Adafruit_HUZZAH_ESP8266_Breakout1 = Adafruit HUZZAH ESP8266 Breakout [part_number=2471]
  BUTTON = Pushbutton [package="[THT]"]
  LED1 = RGB LED (com. cathode, rgb) [package="5 mm [THT]"]
  TOGGLE = Toggle Switch [package=THT]
  U1 = POT [package=pot_mammoth]
  BUZZER = Piezo Speaker
  R1 = Resistor [tolerance=±5% resistance=1k package=THT]
  R2 = Resistor [tolerance=±5% resistance=220 package=THT]
  R3 = Resistor [tolerance=±5% resistance=220 package=THT]
  R4 = Resistor [tolerance=±5% resistance=560 package=THT]
  VCC3 = 4 x AAA Battery Mount
  ELECTROMAGNET = Solenoid
  R5 = Resistor [tolerance=±5% resistance=10k package=THT]
  R6 = Resistor [tolerance=±5% resistance=10k package=THT]

nets:
  N1: Adafruit_HUZZAH_ESP8266_Breakout1.GND, U1.A, BUZZER.pin2, R1.Pin_0, R2.Pin_1, R3.Pin_0, VCC3.+, ELECTROMAGNET.pin2, R5.Pin_0, R6.Pin_0
  N2: Adafruit_HUZZAH_ESP8266_Breakout1.VBat, VCC3.-
  N3: Adafruit_HUZZAH_ESP8266_Breakout1.#13, LED1.red_anode
  N4: Adafruit_HUZZAH_ESP8266_Breakout1.#12, LED1.blue_anode
  N5: Adafruit_HUZZAH_ESP8266_Breakout1.#14, ELECTROMAGNET.pin1
  N6: Adafruit_HUZZAH_ESP8266_Breakout1.#16, BUTTON.Pin_4, R1.Pin_1
  N7: Adafruit_HUZZAH_ESP8266_Breakout1.A, U1.S
  N8: Adafruit_HUZZAH_ESP8266_Breakout1.#5, TOGGLE.L2, R5.Pin_1
  N9: Adafruit_HUZZAH_ESP8266_Breakout1.#4, TOGGLE.L1, R6.Pin_1
  N10: Adafruit_HUZZAH_ESP8266_Breakout1.#15, BUZZER.pin1
  N11: Adafruit_HUZZAH_ESP8266_Breakout1.3V, BUTTON.Pin_1, BUTTON.Pin_2, TOGGLE.COM, R4.Pin_0
  N12: LED1.common_cathode, R2.Pin_0
  N13: U1.E, R3.Pin_1, R4.Pin_1
